// Logisim project systolic_4x4_auto.circ as structural Verilog: 4 circuits, main circuit main
module main (
  input  [7:0] col0,
  input  [7:0] col1,
  input  clk,
  input  clear,
  input  [7:0] row0,
  input  [7:0] row1
);

  wire [7:0] pe_1_a_out, pe_1_b_out, pe_2_a_out, pe_3_b_out;
  wire [19:0] pe_1_acc, pe_2_acc, pe_3_acc, pe_4_acc;

  PE pe_1 (.clk(clk), .clear(clear), .a_in(row0), .b_in(col0), .a_out(pe_1_a_out), .b_out(pe_1_b_out), .acc(pe_1_acc));
  // Probe on pe_1_acc
  PE pe_2 (
    .clk(clk), .clear(clear), .a_in(row1), .b_in(pe_1_b_out), .a_out(pe_2_a_out), .acc(pe_2_acc));  // open: b_out
  // Probe on pe_2_acc
  PE pe_3 (
    .clk(clk), .clear(clear), .a_in(pe_1_a_out), .b_in(col1), .b_out(pe_3_b_out), .acc(pe_3_acc));  // open: a_out
  // Probe on pe_3_acc
  PE pe_4 (.clk(clk), .clear(clear), .a_in(pe_2_a_out), .b_in(pe_3_b_out), .acc(pe_4_acc));  // open: a_out, b_out
  // Probe on pe_4_acc
endmodule

module PE (
  input  clk,
  input  clear,
  input  [7:0] a_in,
  input  [7:0] b_in,
  output [7:0] a_out,
  output [7:0] b_out,
  output [19:0] acc
);

  wire [19:0] adder_1_out, bit_extender_1_out, bit_extender_2_out, multiplier_1_out;

  Register a_reg (.D(a_in), .en(1'b1), .clk(clk), .Q(a_out), .clr(clear));
  Register b_reg (.D(b_in), .en(1'b1), .clk(clk), .Q(b_out), .clr(clear));
  assign bit_extender_1_out = {{12{1'b0}}, a_in};  // Bit_Extender bit_extender_1
  assign bit_extender_2_out = {{12{1'b0}}, b_in};  // Bit_Extender bit_extender_2
  Multiplier #(.width(20)) multiplier_1 (
    .a(bit_extender_1_out), .b(bit_extender_2_out), .out(multiplier_1_out));  // open: cin, cout
  Adder #(.width(20)) adder_1 (.a(multiplier_1_out), .b(acc), .out(adder_1_out), .cin(1'b0));  // open: cout
  Register #(.width(20)) acc_reg (.D(adder_1_out), .en(1'b1), .clk(clk), .Q(acc), .clr(clear));
endmodule

module main_4X4 (
  input  [7:0] col0,
  input  [7:0] col1,
  input  [7:0] col2,
  input  [7:0] col3,
  input  clk,
  input  clear,
  input  [7:0] row0,
  input  [7:0] row1,
  input  [7:0] row2,
  input  [7:0] row3
);

  wire [7:0] PE00_a_out, PE00_b_out, PE01_a_out, PE01_b_out, PE02_a_out, PE02_b_out, PE03_b_out, PE10_a_out,
       PE10_b_out, PE11_a_out, PE11_b_out, PE12_a_out, PE12_b_out, PE13_b_out, PE20_a_out, PE20_b_out,
       PE21_a_out, PE21_b_out, PE22_a_out, PE22_b_out, PE23_b_out, PE30_a_out, PE31_a_out, PE32_a_out,
       register_1_q, register_2_q, register_3_q, register_4_q, register_5_q, register_6_q, register_7_q,
       register_8_q, register_9_q, register_10_q, register_11_q, register_12_q, rom_1_data, rom_2_data,
       rom_3_data, rom_4_data, rom_5_data, rom_6_data, rom_7_data;
  wire [19:0] PE00_acc, PE01_acc, PE02_acc, PE03_acc, PE10_acc, PE11_acc, PE12_acc, PE13_acc, PE20_acc,
       PE21_acc, PE22_acc, PE23_acc, PE30_acc, PE31_acc, PE32_acc, PE33_acc;

  ROM #(.addrWidth(4)) rom_1 (.data(rom_1_data));  // open: addr
  ROM #(.addrWidth(4)) rom_2 (.data(rom_2_data));  // open: addr
  ROM #(.addrWidth(4)) rom_3 (.data(rom_3_data));  // open: addr
  ROM #(.addrWidth(4)) rom_4 (.data(rom_4_data));  // open: addr
  Register register_1 (.D(row3), .en(1'b1), .clk(clear), .Q(register_1_q), .clr(clear));
  ROM #(.addrWidth(4)) rom_5 (.data(rom_5_data));  // open: addr
  Register register_2 (.D(row1), .en(1'b1), .clk(clear), .Q(register_2_q), .clr(clear));
  Register register_3 (.D(row2), .en(1'b1), .clk(clear), .Q(register_3_q), .clr(clear));
  Register register_4 (.D(register_1_q), .en(1'b1), .clk(clear), .Q(register_4_q), .clr(clear));
  Register register_5 (.D(register_3_q), .clk(clear), .Q(register_5_q), .clr(clear));  // open: en
  Register register_6 (.D(register_4_q), .en(1'b1), .clk(clear), .Q(register_6_q), .clr(clear));
  ROM #(.addrWidth(4)) rom_6 (.data(rom_6_data));  // open: addr
  PE PE20 (
    .clk(clear), .clear(clear), .a_in(register_5_q), .b_in(PE10_b_out), .a_out(PE20_a_out),
    .b_out(PE20_b_out), .acc(PE20_acc));
  PE PE30 (
    .clk(clear), .clear(clear), .a_in(register_6_q), .b_in(PE20_b_out), .a_out(PE30_a_out), .acc(PE30_acc));  // open: b_out
  PE PE00 (
    .clk(clear), .clear(clear), .a_in(row0), .b_in(col0), .a_out(PE00_a_out), .b_out(PE00_b_out),
    .acc(PE00_acc));
  // Probe on PE00_acc
  PE PE10 (
    .clk(clear), .clear(clear), .a_in(register_2_q), .b_in(PE00_b_out), .a_out(PE10_a_out),
    .b_out(PE10_b_out), .acc(PE10_acc));
  // Probe on PE10_acc
  // Probe on PE20_acc
  // Probe on PE30_acc
  ROM #(.addrWidth(4)) rom_7 (.data(rom_7_data));  // open: addr
  Register register_7 (.D(col1), .en(1'b1), .clk(clear), .Q(register_7_q), .clr(clear));
  PE PE21 (
    .clk(clear), .clear(clear), .a_in(PE20_a_out), .b_in(PE11_b_out), .a_out(PE21_a_out), .b_out(PE21_b_out),
    .acc(PE21_acc));
  PE PE31 (
    .clk(clear), .clear(clear), .a_in(PE30_a_out), .b_in(PE21_b_out), .a_out(PE31_a_out), .acc(PE31_acc));  // open: b_out
  PE PE01 (
    .clk(clear), .clear(clear), .a_in(PE00_a_out), .b_in(register_7_q), .a_out(PE01_a_out),
    .b_out(PE01_b_out), .acc(PE01_acc));
  PE PE11 (
    .clk(clear), .clear(clear), .a_in(PE10_a_out), .b_in(PE01_b_out), .a_out(PE11_a_out), .b_out(PE11_b_out),
    .acc(PE11_acc));
  // Probe on PE31_acc
  Register register_8 (.D(col2), .en(1'b1), .clk(clear), .Q(register_8_q), .clr(clear));
  // Probe on PE01_acc
  // Probe on PE11_acc
  // Probe on PE21_acc
  ROM #(.addrWidth(4)) rom_8 ();  // open: addr, data
  Register register_9 (.D(register_8_q), .en(1'b1), .clk(clear), .Q(register_9_q), .clr(clear));
  PE PE22 (
    .clk(clear), .clear(clear), .a_in(PE21_a_out), .b_in(PE12_b_out), .a_out(PE22_a_out), .b_out(PE22_b_out),
    .acc(PE22_acc));
  PE PE32 (
    .clk(clear), .clear(clear), .a_in(PE31_a_out), .b_in(PE22_b_out), .a_out(PE32_a_out), .acc(PE32_acc));  // open: b_out
  PE PE02 (
    .clk(clear), .clear(clear), .a_in(PE01_a_out), .b_in(register_9_q), .a_out(PE02_a_out),
    .b_out(PE02_b_out), .acc(PE02_acc));
  PE PE12 (
    .clk(clear), .clear(clear), .a_in(PE11_a_out), .b_in(PE02_b_out), .a_out(PE12_a_out), .b_out(PE12_b_out),
    .acc(PE12_acc));
  // Probe on PE22_acc
  // Probe on PE32_acc
  // Probe on PE02_acc
  // Probe on PE12_acc
  Register register_10 (.D(col3), .en(1'b1), .clk(clear), .Q(register_10_q), .clr(clear));
  Register register_11 (.D(register_10_q), .en(1'b1), .clk(clear), .Q(register_11_q), .clr(clear));
  Register register_12 (.D(register_11_q), .en(1'b1), .clk(clear), .Q(register_12_q), .clr(clear));
  PE PE23 (
    .clk(clear), .clear(clear), .a_in(PE22_a_out), .b_in(PE13_b_out), .b_out(PE23_b_out), .acc(PE23_acc));  // open: a_out
  PE PE33 (.clk(clear), .clear(clear), .a_in(PE32_a_out), .b_in(PE23_b_out), .acc(PE33_acc));  // open: a_out, b_out
  PE PE03 (
    .clk(clear), .clear(clear), .a_in(PE02_a_out), .b_in(register_12_q), .b_out(PE03_b_out), .acc(PE03_acc));  // open: a_out
  PE PE13 (
    .clk(clear), .clear(clear), .a_in(PE12_a_out), .b_in(PE03_b_out), .b_out(PE13_b_out), .acc(PE13_acc));  // open: a_out
  // Probe on PE03_acc
  // Probe on PE13_acc
  // Probe on PE23_acc
  // Probe on PE33_acc

  assign clk = clear;

  // Notes on the sheet:
  //   contents of rom_1 (hex, n*v repeats v):
  //   1 2 3 4
  //   contents of rom_2 (hex, n*v repeats v):
  //   5 6 7 8
  //   contents of rom_3 (hex, n*v repeats v):
  //   d 9 5 1
  //   contents of rom_4 (hex, n*v repeats v):
  //   d 9 5 1
  //   contents of rom_5 (hex, n*v repeats v):
  //   d 9 5 1
  //   contents of rom_6 (hex, n*v repeats v):
  //   d 9 5 1
  //   contents of rom_7 (hex, n*v repeats v):
  //   d 9 5 1
  //   contents of rom_8 (hex, n*v repeats v):
  //   d 9 5 1
endmodule

module main_4X4_auto (
  input  Start,
  output done
);

  wire busy, clear, clk, not_done_out, not_run_out, run_D_or_out, run_q;
  wire [3:0] t;
  wire [7:0] PE00_a_out, PE00_b_out, PE01_a_out, PE01_b_out, PE02_a_out, PE02_b_out, PE03_b_out, PE10_a_out,
       PE10_b_out, PE11_a_out, PE11_b_out, PE12_a_out, PE12_b_out, PE13_b_out, PE20_a_out, PE20_b_out,
       PE21_a_out, PE21_b_out, PE22_a_out, PE22_b_out, PE23_b_out, PE30_a_out, PE31_a_out, PE32_a_out,
       register_1_q, register_2_q, register_3_q, register_4_q, register_5_q, register_6_q, register_7_q,
       register_8_q, register_9_q, register_10_q, register_11_q, register_12_q, rom_1_data, rom_2_data,
       rom_3_data, rom_4_data, rom_5_data, rom_6_data, rom_7_data, rom_8_data;
  wire [19:0] PE00_acc, PE01_acc, PE02_acc, PE03_acc, PE10_acc, PE11_acc, PE12_acc, PE13_acc, PE20_acc,
       PE21_acc, PE22_acc, PE23_acc, PE30_acc, PE31_acc, PE32_acc, PE33_acc;

  or run_D_or (run_D_or_out, Start, busy);
  Register #(.width(1)) run (.D(run_D_or_out), .en(1'b1), .clk(clk), .Q(run_q));  // open: clr
  not not_run (not_run_out, run_q);
  not not_done (not_done_out, done);
  ROM #(.addrWidth(4)) rom_1 (.addr(t), .data(rom_1_data));
  and clear_and (clear, Start, not_run_out);
  and busy_and (busy, run_q, not_done_out);
  ROM #(.addrWidth(4)) rom_2 (.addr(t), .data(rom_2_data));
  ROM #(.addrWidth(4)) rom_3 (.addr(t), .data(rom_3_data));
  ROM #(.addrWidth(4)) rom_4 (.addr(t), .data(rom_4_data));
  Counter #(.max('hf), .width(4)) t_counter (.count(busy), .Q(t), .clk(clk), .clr(clear));  // open: load, D, carry, up
  Comparator #(.mode("unsigned"), .width(4)) comparator_1 (.a(t), .b(4'b1010), .eq(done));  // open: gt, lt
  LED done_led (.in(done));
  Hex_Digit_Display t_display (.value(t));  // open: dp
  Clock u_clk (.out(clk));
  Register register_1 (.D(rom_4_data), .en(1'b1), .clk(clk), .Q(register_1_q), .clr(clear));
  ROM #(.addrWidth(4)) rom_5 (.addr(t), .data(rom_5_data));
  Register register_2 (.D(rom_2_data), .en(1'b1), .clk(clk), .Q(register_2_q), .clr(clear));
  Register register_3 (.D(rom_3_data), .en(1'b1), .clk(clk), .Q(register_3_q), .clr(clear));
  Register register_4 (.D(register_1_q), .en(1'b1), .clk(clk), .Q(register_4_q), .clr(clear));
  Register register_5 (.D(register_3_q), .clk(clk), .Q(register_5_q), .clr(clear));  // open: en
  Register register_6 (.D(register_4_q), .en(1'b1), .clk(clk), .Q(register_6_q), .clr(clear));
  ROM #(.addrWidth(4)) rom_6 (.addr(t), .data(rom_6_data));
  PE PE20 (
    .clk(clk), .clear(clear), .a_in(register_5_q), .b_in(PE10_b_out), .a_out(PE20_a_out), .b_out(PE20_b_out),
    .acc(PE20_acc));
  PE PE30 (
    .clk(clk), .clear(clear), .a_in(register_6_q), .b_in(PE20_b_out), .a_out(PE30_a_out), .acc(PE30_acc));  // open: b_out
  PE PE00 (
    .clk(clk), .clear(clear), .a_in(rom_1_data), .b_in(rom_5_data), .a_out(PE00_a_out), .b_out(PE00_b_out),
    .acc(PE00_acc));
  // Probe on PE00_acc
  PE PE10 (
    .clk(clk), .clear(clear), .a_in(register_2_q), .b_in(PE00_b_out), .a_out(PE10_a_out), .b_out(PE10_b_out),
    .acc(PE10_acc));
  // Probe on PE10_acc
  // Probe on PE20_acc
  // Probe on PE30_acc
  ROM #(.addrWidth(4)) rom_7 (.addr(t), .data(rom_7_data));
  Register register_7 (.D(rom_6_data), .en(1'b1), .clk(clk), .Q(register_7_q), .clr(clear));
  PE PE21 (
    .clk(clk), .clear(clear), .a_in(PE20_a_out), .b_in(PE11_b_out), .a_out(PE21_a_out), .b_out(PE21_b_out),
    .acc(PE21_acc));
  PE PE31 (
    .clk(clk), .clear(clear), .a_in(PE30_a_out), .b_in(PE21_b_out), .a_out(PE31_a_out), .acc(PE31_acc));  // open: b_out
  PE PE01 (
    .clk(clk), .clear(clear), .a_in(PE00_a_out), .b_in(register_7_q), .a_out(PE01_a_out), .b_out(PE01_b_out),
    .acc(PE01_acc));
  PE PE11 (
    .clk(clk), .clear(clear), .a_in(PE10_a_out), .b_in(PE01_b_out), .a_out(PE11_a_out), .b_out(PE11_b_out),
    .acc(PE11_acc));
  // Probe on PE31_acc
  Register register_8 (.D(rom_7_data), .en(1'b1), .clk(clk), .Q(register_8_q), .clr(clear));
  // Probe on PE01_acc
  // Probe on PE11_acc
  // Probe on PE21_acc
  ROM #(.addrWidth(4)) rom_8 (.addr(t), .data(rom_8_data));
  Register register_9 (.D(register_8_q), .en(1'b1), .clk(clk), .Q(register_9_q), .clr(clear));
  PE PE22 (
    .clk(clk), .clear(clear), .a_in(PE21_a_out), .b_in(PE12_b_out), .a_out(PE22_a_out), .b_out(PE22_b_out),
    .acc(PE22_acc));
  PE PE32 (
    .clk(clk), .clear(clear), .a_in(PE31_a_out), .b_in(PE22_b_out), .a_out(PE32_a_out), .acc(PE32_acc));  // open: b_out
  PE PE02 (
    .clk(clk), .clear(clear), .a_in(PE01_a_out), .b_in(register_9_q), .a_out(PE02_a_out), .b_out(PE02_b_out),
    .acc(PE02_acc));
  PE PE12 (
    .clk(clk), .clear(clear), .a_in(PE11_a_out), .b_in(PE02_b_out), .a_out(PE12_a_out), .b_out(PE12_b_out),
    .acc(PE12_acc));
  // Probe on PE22_acc
  // Probe on PE32_acc
  // Probe on PE02_acc
  // Probe on PE12_acc
  Register register_10 (.D(rom_8_data), .en(1'b1), .clk(clk), .Q(register_10_q), .clr(clear));
  Register register_11 (.D(register_10_q), .en(1'b1), .clk(clk), .Q(register_11_q), .clr(clear));
  Register register_12 (.D(register_11_q), .en(1'b1), .clk(clk), .Q(register_12_q), .clr(clear));
  PE PE23 (
    .clk(clk), .clear(clear), .a_in(PE22_a_out), .b_in(PE13_b_out), .b_out(PE23_b_out), .acc(PE23_acc));  // open: a_out
  PE PE33 (.clk(clk), .clear(clear), .a_in(PE32_a_out), .b_in(PE23_b_out), .acc(PE33_acc));  // open: a_out, b_out
  PE PE03 (
    .clk(clk), .clear(clear), .a_in(PE02_a_out), .b_in(register_12_q), .b_out(PE03_b_out), .acc(PE03_acc));  // open: a_out
  PE PE13 (
    .clk(clk), .clear(clear), .a_in(PE12_a_out), .b_in(PE03_b_out), .b_out(PE13_b_out), .acc(PE13_acc));  // open: a_out
  // Probe on PE03_acc
  // Probe on PE13_acc
  // Probe on PE23_acc
  // Probe on PE33_acc

  // Notes on the sheet:
  //   contents of rom_1 (hex, n*v repeats v):
  //   1 2 3 4
  //   contents of rom_2 (hex, n*v repeats v):
  //   5 6 7 8
  //   contents of rom_3 (hex, n*v repeats v):
  //   9 a b c
  //   contents of rom_4 (hex, n*v repeats v):
  //   d e f 10
  //   contents of rom_5 (hex, n*v repeats v):
  //   10 c 8 4
  //   contents of rom_6 (hex, n*v repeats v):
  //   f b 7 3
  //   contents of rom_7 (hex, n*v repeats v):
  //   e a 6 2
  //   contents of rom_8 (hex, n*v repeats v):
  //   d 9 5 1
endmodule
